# Fritzing sketch rpi3_schematics (saved by Fritzing 0.9.3b)
breadboards: 1

parts:
  Raspberry_Pi_1 = Raspberry Pi 3 [part_number=RPI-3-V1.2]
  Part1 = Adafruit ADS1015 12Bit I2C ADC [part_number="Adafruit #1083"]
  U1 = POT [package=pot_mammoth]

nets:
  N1: Raspberry_Pi_1.GPIO2, Part1.SDA
  N2: Raspberry_Pi_1.GPIO3, Part1.SCL
  GND: Raspberry_Pi_1.GND, Part1.AIN1, Part1.GND, U1.S
  5V: Raspberry_Pi_1.5V, Part1.VDD, U1.E
  N3: Part1.AIN0, U1.A

custom parts:
  Adafruit ADS1015 12Bit I2C ADC: For microcontrollers without an analog-to-digital converter or when you want a higher-precision ADC, the ADS1015 provides 12-bit precision at 3300 samples/second over I2C. The chip can be configured as 4 single-ended input channels, or two differential channels. As a nice bonus, it even includes a programmable gain amplifier, up to x16, to help boost up smaller single/differential signals to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
