# Fritzing sketch edison_schematics (saved by Fritzing 0.9.3b)

parts:
  Part1 = Intel Edison Arduinobreakout
  LPD8806_RGB_LED_Strip2 = LPD8806 RGB LED Strip

nets:
  N1: Part1.D11_PWM/MOSI, LPD8806_RGB_LED_Strip2.DI
  N2: Part1.D13/SCK, LPD8806_RGB_LED_Strip2.CI
  GND: Part1.GND, LPD8806_RGB_LED_Strip2.GND
  5V: Part1.5V, LPD8806_RGB_LED_Strip2.+5V

custom parts:
  LPD8806 RGB LED Strip: Digitally addressable RGB LED strip
