# Fritzing sketch rpi3_schematics (saved by Fritzing 0.9.3b)

parts:
  LPD8806_RGB_LED_Strip2 = LPD8806 RGB LED Strip
  Raspberry_Pi_1 = Raspberry Pi 3 [part_number=RPI-3-V1.2]

nets:
  GND: LPD8806_RGB_LED_Strip2.GND, Raspberry_Pi_1.GND
  N1: LPD8806_RGB_LED_Strip2.DI, Raspberry_Pi_1.GPIO10
  N2: LPD8806_RGB_LED_Strip2.CI, Raspberry_Pi_1.GPIO11
  +5V: LPD8806_RGB_LED_Strip2.+5V, Raspberry_Pi_1.5V

custom parts:
  LPD8806 RGB LED Strip: Digitally addressable RGB LED strip
