# Fritzing sketch edison_schematics (saved by Fritzing 0.9.3b)
breadboards: 1

parts:
  Part1 = Intel Edison Arduinobreakout
  Part2 = Adafruit_BMP280

nets:
  GND: Part1.GND, Part2.GND
  N1: Part1.A4/SDA, Part2.SDI/SDA
  N2: Part1.A5/SCL, Part2.SCK/SCL
  5V: Part1.5V, Part2.VIN

custom parts:
  Adafruit_BMP280: Bosch has stepped up their game with their new BMP280 sensor, an environmental sensor with temperature, barometric pressure that is the next generation upgrade to the BMP085/BMP180/BMP183. This sensor is great for all sorts of weather sensing and can even be used in both I2C and SPI! This precision sensor from Bosch is the best low-cost, precision sensing solution for measuring barometric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
