# Fritzing sketch edison_schematics (saved by Fritzing 0.9.3b)
breadboards: 1

parts:
  Part1 = Intel Edison Arduinobreakout
  Part2 = 0.56" 7-segment LED Backpack [part_number=881]

nets:
  GND: Part1.GND, Part2.GND
  N1: Part1.A4/SDA, Part2.SDA
  N2: Part1.A5/SCL, Part2.SCL
  3V3: Part1.3V3, Part2.VDD

custom parts:
  0.56" 7-segment LED Backpack: This 0.56" 7-segment LED display includes a driver chip for simple control via an I2C interface. The backpack features address-selection jumpers so you can connect up to eight displays on a single I2C bus.
