# Fritzing sketch rpi3_schematics (saved by Fritzing 0.9.3b)
breadboards: 1

parts:
  Raspberry_Pi_1 = Raspberry Pi 3 [part_number=RPI-3-V1.2]
  Part3 = 0.56" 7-segment LED Backpack [part_number=881]

nets:
  3V3: Raspberry_Pi_1.3v3, Part3.VDD
  N1: Raspberry_Pi_1.GPIO2, Part3.SDA
  N2: Raspberry_Pi_1.GPIO3, Part3.SCL
  GND: Raspberry_Pi_1.GND, Part3.GND

custom parts:
  0.56" 7-segment LED Backpack: This 0.56" 7-segment LED display includes a driver chip for simple control via an I2C interface. The backpack features address-selection jumpers so you can connect up to eight displays on a single I2C bus.
