# Fritzing sketch rpi3_schematics (saved by Fritzing 0.9.3b)
breadboards: 1

parts:
  Raspberry_Pi_1 = Raspberry Pi 3 [part_number=RPI-3-V1.2]
  IC1 = IC, SIP package, 7 pins [chip_label=KEYPAD]
  R1 = Resistor [tolerance=±5% resistance=220 package=THT]
  R2 = Resistor [tolerance=±5% resistance=220 package=THT]
  R3 = Resistor [tolerance=±5% resistance=220 package=THT]
  R4 = Resistor [tolerance=±5% resistance=220 package=THT]

nets:
  N1: Raspberry_Pi_1.GIPO27, IC1.pin1, R3.Pin_1
  N2: Raspberry_Pi_1.GIPO5, IC1.pin2, R1.Pin_1
  N3: Raspberry_Pi_1.GIPO6, IC1.pin3, R2.Pin_1
  N4: Raspberry_Pi_1.GIPO26, IC1.pin4, R4.Pin_1
  N5: Raspberry_Pi_1.GIPO16, IC1.pin5
  N6: Raspberry_Pi_1.GND, R1.Pin_0, R2.Pin_0, R3.Pin_0, R4.Pin_0
  N7: Raspberry_Pi_1.GIPO24, IC1.pin6
  N8: Raspberry_Pi_1.GIPO23, IC1.pin7
