# Fritzing sketch edison_schematics (saved by Fritzing 0.9.3b)

parts:
  Grove1 = Grove 3 Axis Digital Accelerometer 16g
  Part1 = Intel Edison Arduinobreakout

nets:
  GND: Grove1.GND, Part1.GND
  VCC: Grove1.VCC, Part1.5V
  N1: Grove1.SDA, Part1.A4/SDA
  N2: Grove1.SCL, Part1.A5/SCL
