# Fritzing sketch rpi3_schematics (saved by Fritzing 0.9.3b)

parts:
  Raspberry_Pi_1 = Raspberry Pi 3 [part_number=RPI-3-V1.2]
  Grove1 = Grove 3 Axis Digital Accelerometer 16g

nets:
  N1: Raspberry_Pi_1.GPIO2, Grove1.SDA
  N2: Raspberry_Pi_1.GPIO3, Grove1.SCL
  GND: Raspberry_Pi_1.GND, Grove1.GND
  5V: Raspberry_Pi_1.5V, Grove1.VCC
