# Fritzing sketch edison_schematics (saved by Fritzing 0.9.3b)
breadboards: 1

parts:
  J1 = Piezo Speaker
  Part1 = Intel Edison Arduinobreakout

nets:
  N1: J1.pin1, Part1.GND
  N2: J1.pin2, Part1.D3_PWM
