# Fritzing sketch edison_schematics (saved by Fritzing 0.9.3b)

parts:
  Part1 = Intel Edison Arduinobreakout
  Squix1 = OLED 0.96" 128x64 I2C SSD1306

nets:
  N1: Part1.A4/SDA, Squix1.SCA
  N2: Part1.A5/SCL, Squix1.SCL
  5V: Part1.5V, Squix1.VCC
  GND: Part1.GND, Squix1.GND
