# Fritzing sketch rpi3_schematics (saved by Fritzing 0.9.3b)

parts:
  Squix1 = OLED 0.96" 128x64 I2C SSD1306
  Raspberry_Pi_1 = Raspberry Pi 3 [part_number=RPI-3-V1.2]

nets:
  VCC: Squix1.VCC, Raspberry_Pi_1.5V
  GND: Squix1.GND, Raspberry_Pi_1.GND
  N1: Squix1.SCL, Raspberry_Pi_1.GPIO3
  N2: Squix1.SCA, Raspberry_Pi_1.GPIO2
