# Fritzing sketch edison_schematics (saved by Fritzing 0.9.3b)

parts:
  Grove1 = Grove 4 Digit Display
  Part1 = Intel Edison Arduinobreakout

nets:
  GND: Grove1.GND, Part1.GND
  VCC: Grove1.VCC, Part1.5V
  N1: Grove1.DIO, Part1.D7
  N2: Grove1.CLK, Part1.D6_PWM
